// Logisim project comp.circ as structural Verilog: 1 circuit, main circuit main
module main (
);

  wire and_1_out, and_2_out, and_3_out, and_4_out, and_5_out, and_6_out, and_7_out, and_8_out, and_10_out,
       clock_1_out, comparator_1_eq, comparator_2_eq, comparator_2_gt, comparator_2_lt, decoder_1_out0,
       decoder_1_out1, decoder_1_out2, decoder_1_out3, decoder_1_out4, decoder_2_out0, decoder_2_out1,
       decoder_3_out0, decoder_3_out1, decoder_3_out2, decoder_3_out3, decoder_4_out0, decoder_4_out1,
       decoder_4_out2, decoder_5_out3, not_1_out, not_2_out, not_3_out, or_1_out, or_2_out,
       pull_resistor_1_node;
  wire [1:0] INST_q, multiplexer_2_out;
  wire [2:0] counter_1_q;
  wire [3:0] multiplexer_4_out;
  wire [3:2] INST_q_2;
  wire [7:0] ACC_2_q, ACC_q, adder_1_out, adder_2_out, and_9_out, INST_q_3, multiplexer_1_out,
       multiplexer_3_out, multiplexer_5_out, not_4_out, or_3_out, ram_1_data, REGA_q, REGB_q, REGC_q,
       register_1_q, register_2_q, rom_1_data, xor_1_out;

  Clock clock_1 (.out(clock_1_out));
  and and_1 (and_1_out, clock_1_out, not_1_out);
  Comparator comparator_1 (.a({8{1'b1}}), .b(register_2_q), .eq(comparator_1_eq));  // open: gt, lt
  Adder adder_1 (.a(8'h1), .b(register_2_q), .out(adder_1_out));  // open: cin, cout
  Register register_1 (.D(adder_1_out), .Q(register_1_q), .clk(decoder_1_out2));  // open: en, clr
  Counter #(.width(3), .max('h4)) counter_1 (.Q(counter_1_q), .clk(and_1_out));  // open: load, D, count, carry, clr
  not not_1 (not_1_out, comparator_1_eq);
  Multiplexer #(.width(8)) multiplexer_1 (
    .in0(register_1_q), .in1(ACC_2_q), .out(multiplexer_1_out), .sel(and_2_out));  // open: en
  Decoder #(.select(3)) decoder_1 (
    .out0(decoder_1_out0), .out1(decoder_1_out1), .out2(decoder_1_out2), .out3(decoder_1_out3),
    .out4(decoder_1_out4), .sel(counter_1_q));  // open: out5, out6, out7, en
  Register register_2 (.D(multiplexer_1_out), .Q(register_2_q), .clk(decoder_1_out0));  // open: en, clr
  Register INST (.D(rom_1_data), .Q({INST_q_2, INST_q_3[3:0], INST_q}), .clk(decoder_1_out1));  // open: en, clr
  Register ACC (.D(ACC_2_q), .Q(ACC_q), .clk(decoder_1_out0));  // open: en, clr
  ROM rom_1 (.addr(register_2_q), .data(rom_1_data));  // open: sel
  and and_2 (and_2_out, or_1_out, pull_resistor_1_node);
  Pull_Resistor pull_resistor_1 (.node(pull_resistor_1_node));
  not not_2 (not_2_out, comparator_2_eq);
  Comparator #(.mode("unsigned")) comparator_2 (
    .a(ACC_q), .b({8{1'b0}}), .gt(comparator_2_gt), .eq(comparator_2_eq), .lt(comparator_2_lt));
  Decoder #(.select(4), .disabled(0)) decoder_2 (
    .out0(decoder_2_out0), .out1(decoder_2_out1), .sel({INST_q_2, INST_q_3[3:2]}));  // open: out2, out3, out4, out5, out6, out7, out8, out9, out10, out11, out12, out13, out14, out15, en
  // Probe on INST_q_3
  // Probe on {INST_q_3[3:0], multiplexer_4_out}
  or or_1 (or_1_out, and_3_out, and_4_out, and_6_out, and_5_out);
  and and_3 (and_3_out, comparator_2_lt, decoder_3_out3);
  and and_4 (and_4_out, comparator_2_gt, decoder_3_out2);
  Register REGA (.D(ACC_2_q), .Q(REGA_q), .clk(decoder_4_out0));  // open: en, clr
  Register REGB (.D(ACC_2_q), .Q(REGB_q), .clk(decoder_4_out1));  // open: en, clr
  Register REGC (.D(ACC_2_q), .Q(REGC_q), .clk(decoder_4_out2));  // open: en, clr
  and and_5 (and_5_out, comparator_2_eq, decoder_3_out0);
  and and_6 (and_6_out, not_2_out, decoder_3_out1);
  Decoder #(.select(2), .disabled(0)) decoder_3 (
    .out0(decoder_3_out0), .out1(decoder_3_out1), .out2(decoder_3_out2), .out3(decoder_3_out3),
    .sel(INST_q_3[1:0]));  // open: en
  Multiplexer #(.width(2)) multiplexer_2 (
    .in0(INST_q_3[1:0]), .in1(2'b10), .out(multiplexer_2_out), .sel(decoder_5_out3));  // open: en
  Decoder #(.select(2), .tristate("true"), .disabled(0)) decoder_4 (
    .out0(decoder_4_out0), .out1(decoder_4_out1), .out2(decoder_4_out2), .out3(pull_resistor_1_node),
    .sel(INST_q), .en(and_8_out));
  Decoder #(.select(2), .disabled(0)) decoder_5 (.out3(decoder_5_out3), .sel(INST_q));  // open: out0, out1, out2, en
  // Probe on multiplexer_3_out
  Multiplexer #(.select(2), .width(8)) multiplexer_3 (
    .in0(REGA_q), .in1(REGB_q), .in2(REGC_q), .in3(register_2_q), .out(multiplexer_3_out),
    .sel(multiplexer_2_out));  // open: en
  Multiplexer #(.select(2), .width(8)) multiplexer_4 (
    .in0(REGA_q), .in1(REGB_q), .in2(REGC_q), .in3(register_2_q), .out({INST_q_3[7:4], multiplexer_4_out}),
    .sel(INST_q));  // open: en
  and and_7 (and_7_out, decoder_1_out2, decoder_2_out0);
  and and_8 (and_8_out, decoder_1_out4, not_3_out);
  not not_3 (not_3_out, decoder_2_out1);
  RAM #(.bus("separate")) ram_1 (
    .addr(multiplexer_3_out), .din(ACC_2_q), .data(ram_1_data), .str(decoder_2_out1), .clk(or_2_out),
    .ld(decoder_2_out0));  // open: sel, clr
  or or_2 (or_2_out, and_7_out, and_10_out);
  assign and_9_out = multiplexer_3_out & {INST_q_3[7:4], multiplexer_4_out};  // AND_Gate and_9, 8 bits wide
  assign or_3_out = multiplexer_3_out | {INST_q_3[7:4], multiplexer_4_out};  // OR_Gate or_3, 8 bits wide
  Adder adder_2 (.a(multiplexer_3_out), .b({INST_q_3[7:4], multiplexer_4_out}), .out(adder_2_out));  // open: cin, cout
  assign not_4_out = ~multiplexer_3_out;  // NOT_Gate not_4, 8 bits wide
  assign xor_1_out = multiplexer_3_out ^ {INST_q_3[7:4], multiplexer_4_out};  // XOR_Gate xor_1, 8 bits wide
  and and_10 (and_10_out, decoder_2_out1, decoder_1_out4);
  // Probe on ram_1_data
  Multiplexer #(.select(4), .width(8)) multiplexer_5 (
    .in0(ram_1_data), .in1({INST_q_3[7:4], multiplexer_4_out}), .in2(and_9_out), .in3(or_3_out),
    .in4(adder_2_out), .in5(not_4_out), .in6(multiplexer_3_out), .in7(xor_1_out), .in8(INST_q_3),
    .in9(INST_q_3), .in10(INST_q_3), .in11(INST_q_3), .in12({INST_q_3[3:0], multiplexer_4_out}),
    .in13({INST_q_3[3:0], multiplexer_4_out}), .in14({INST_q_3[3:0], multiplexer_4_out}),
    .in15({INST_q_3[3:0], multiplexer_4_out}), .out(multiplexer_5_out), .sel({INST_q_2, INST_q_3[3:2]}));  // open: en
  Register ACC_2 (.D(multiplexer_5_out), .Q(ACC_2_q), .clk(decoder_1_out3));  // open: en, clr

  // Notes on the sheet:
  //   contents of rom_1 (hex, n*v repeats v):
  //   8c c0 9a c2 bd fd 44 67 be fe 67
endmodule
