// Logisim project comp.circ as structural Verilog: 1 circuit, main circuit main
// PC
module main (
  output DONE,
  output [15:0] RESULT
);

  wire and_1_out, and_2_out, and_3_out, and_4_out, and_5_out, and_7_out, clock_1_out, comparator_1_eq,
       comparator_2_eq, decoder_1_out0, decoder_1_out1, decoder_1_out2, decoder_1_out3, decoder_2_out5,
       decoder_2_out6, decoder_2_out7, decoder_3_out0, decoder_3_out1, decoder_3_out11, decoder_3_out15,
       decoder_4_out1, decoder_4_out2, decoder_4_out3, decoder_4_out4, decoder_4_out5, decoder_4_out6,
       not_1_out, not_2_out, or_1_out, or_2_out, or_3_out;
  wire [0:0] adder_2_cout;
  wire [1:0] counter_1_q;
  wire [2:0] INST_q_2;
  wire [4:0] INST_q;
  wire [7:0] ACC_q, ACC_T_1_q, adder_1_out, adder_2_out, and_6_out, bit_extender_1_out, bit_extender_2_out,
       D_q, E_q, FLAGS_q, multiplexer_1_out, multiplexer_2_out, multiplexer_3_out, multiplexer_4_out,
       multiplexer_5_out, multiplier_1_out, not_3_out, or_4_out, PC_prime_q, PC_q, ram_1_data, rom_1_data,
       SP_q, xor_1_out;

  Multiplexer #(.width(8)) multiplexer_1 (
    .in0(8'h1), .in1(bit_extender_1_out), .out(multiplexer_1_out), .sel(or_1_out));  // open: en
  Clock clock_1 (.out(clock_1_out));
  Adder adder_1 (.a(PC_q), .b(multiplexer_1_out), .out(adder_1_out));  // open: cin, cout
  Decoder #(.select(2), .disabled(0)) decoder_1 (
    .out0(decoder_1_out0), .out1(decoder_1_out1), .out2(decoder_1_out2), .out3(decoder_1_out3),
    .sel(counter_1_q), .en(not_1_out));
  Counter #(.width(2), .max('h3)) counter_1 (.Q(counter_1_q), .clk(clock_1_out));  // open: load, D, count, carry, clr
  not not_1 (not_1_out, DONE);
  Register PC_prime (.D(multiplexer_2_out), .Q(PC_prime_q), .clk(decoder_1_out3));  // open: en, clr
  Multiplexer #(.width(8)) multiplexer_2 (
    .in0(adder_1_out), .in1(ACC_T_1_q), .out(multiplexer_2_out), .sel(comparator_2_eq));  // open: en
  Register PC (.D(PC_prime_q), .Q(PC_q), .clk(decoder_1_out0));  // open: en, clr
  assign bit_extender_1_out = {{3{INST_q[4]}}, INST_q};  // Bit_Extender bit_extender_1
  Comparator comparator_1 (.a(ACC_T_1_q), .b({8{1'b0}}), .eq(comparator_1_eq));  // open: gt, lt
  and and_1 (and_1_out, comparator_1_eq, decoder_2_out6);
  and and_2 (and_2_out, not_2_out, decoder_2_out7);
  or or_1 (or_1_out, decoder_2_out5, and_1_out, and_2_out);
  Comparator comparator_2 (.a(8'h7), .b({INST_q_2, INST_q}), .eq(comparator_2_eq));  // open: gt, lt
  not not_2 (not_2_out, comparator_1_eq);
  Decoder #(.select(3)) decoder_2 (
    .out5(decoder_2_out5), .out6(decoder_2_out6), .out7(decoder_2_out7), .sel(INST_q_2));  // open: out0, out1, out2, out3, out4, en
  Comparator #(.mode("unsigned")) comparator_3 (.a({8{1'b1}}), .b(PC_q), .eq(DONE));  // open: gt, lt
  Register INST (.D(rom_1_data), .Q({INST_q_2, INST_q}), .clk(decoder_1_out1));  // open: en, clr
  ROM rom_1 (.addr(PC_q), .data(rom_1_data));  // open: sel
  Decoder #(.select(5), .disabled(0)) decoder_3 (
    .out0(decoder_3_out0), .out1(decoder_3_out1), .out11(decoder_3_out11), .out15(decoder_3_out15),
    .sel({INST_q_2, INST_q[4:3]}));  // open: out2, out3, out4, out5, out6, out7, out8, out9, out10, out12, out13, out14, out16, out17, out18, out19, out20, out21, out22, out23, out24, out25, out26, out27, out28, out29, out30, out31, en
  // Probe on INST_q[2:0]
  // Probe on RESULT
  Decoder #(.select(3), .disabled(0)) decoder_4 (
    .out1(decoder_4_out1), .out2(decoder_4_out2), .out3(decoder_4_out3), .out4(decoder_4_out4),
    .out5(decoder_4_out5), .out6(decoder_4_out6), .sel(INST_q[2:0]), .en(and_3_out));  // open: out0, out7
  and and_3 (and_3_out, decoder_3_out0, decoder_1_out3);
  // Probe on RESULT[7:0]
  Register ACC_T_1 (.D(ACC_q), .Q(ACC_T_1_q), .clk(decoder_1_out0));  // open: en, clr
  Register B (.D(ACC_q), .Q(RESULT[7:0]), .clk(decoder_4_out1));  // open: en, clr
  Register C (.D(ACC_q), .Q(RESULT[15:8]), .clk(decoder_4_out2));  // open: en, clr
  Register D (.D(ACC_q), .Q(D_q), .clk(decoder_4_out3));  // open: en, clr
  Register E (.D(ACC_q), .Q(E_q), .clk(decoder_4_out4));  // open: en, clr
  Multiplexer #(.width(8), .enable("false")) multiplexer_3 (
    .in0(ACC_q), .in1({{7{1'b0}}, adder_2_cout[0]}), .out(multiplexer_3_out), .sel(decoder_3_out11));
  or or_2 (or_2_out, decoder_4_out5, and_4_out);
  Register SP (.D(ACC_q), .Q(SP_q), .clk(decoder_4_out6));  // open: en, clr
  assign bit_extender_2_out = {{4{INST_q[3]}}, INST_q[3:0]};  // Bit_Extender bit_extender_2
  Register FLAGS (.D(multiplexer_3_out), .Q(FLAGS_q), .clk(or_2_out));  // open: en, clr
  and and_4 (and_4_out, decoder_3_out11, decoder_1_out3);
  Multiplexer #(.select(3), .width(8)) multiplexer_4 (
    .in0(ACC_T_1_q), .in1(RESULT[7:0]), .in2(RESULT[15:8]), .in3(D_q), .in4(E_q), .in5(FLAGS_q), .in6(SP_q),
    .in7(PC_q), .out(multiplexer_4_out), .sel(INST_q[2:0]));  // open: en
  or or_3 (or_3_out, and_5_out, and_7_out);
  and and_5 (and_5_out, decoder_3_out1, decoder_1_out3);
  assign xor_1_out = multiplexer_4_out ^ ACC_T_1_q;  // XOR_Gate xor_1, 8 bits wide
  assign and_6_out = multiplexer_4_out & ACC_T_1_q;  // AND_Gate and_6, 8 bits wide
  assign or_4_out = multiplexer_4_out | ACC_T_1_q;  // OR_Gate or_4, 8 bits wide
  Adder adder_2 (.a(multiplexer_4_out), .b(ACC_T_1_q), .out(adder_2_out), .cout(adder_2_cout[0]));  // open: cin
  assign not_3_out = ~multiplexer_4_out;  // NOT_Gate not_3, 8 bits wide
  Multiplier multiplier_1 (.a(multiplexer_4_out), .b(ACC_T_1_q), .out(multiplier_1_out));  // open: cin, cout
  RAM #(.bus("separate")) ram_1 (
    .addr(multiplexer_4_out), .din(multiplexer_5_out), .data(ram_1_data), .str(decoder_3_out1),
    .clk(or_3_out), .ld(decoder_3_out15));  // open: sel, clr
  and and_7 (and_7_out, decoder_1_out2, decoder_3_out15);
  // Probe on {INST_q_2, INST_q[4:3]}
  Multiplexer #(.select(5), .width(8)) multiplexer_5 (
    .in0(ACC_T_1_q), .in1(ACC_T_1_q), .in2(ACC_T_1_q), .in3(ACC_T_1_q), .in4(ACC_T_1_q), .in5(ACC_T_1_q),
    .in6(ACC_T_1_q), .in7(ACC_T_1_q), .in8(xor_1_out), .in9(and_6_out), .in10(or_4_out), .in11(adder_2_out),
    .in12(not_3_out), .in13(multiplier_1_out), .in14(multiplexer_4_out), .in15(ram_1_data),
    .in16(bit_extender_2_out), .in17(bit_extender_2_out), .in18({INST_q[3:0], ACC_T_1_q[3:0]}),
    .in19({INST_q[3:0], ACC_T_1_q[3:0]}), .in20(ACC_T_1_q), .in21(ACC_T_1_q), .in22(ACC_T_1_q),
    .in23(ACC_T_1_q), .in24(ACC_T_1_q), .in25(ACC_T_1_q), .in26(ACC_T_1_q), .in27(ACC_T_1_q),
    .in28(ACC_T_1_q), .in29(ACC_T_1_q), .in30(ACC_T_1_q), .in31(ACC_T_1_q), .out(multiplexer_5_out),
    .sel({INST_q_2, INST_q[4:3]}));  // open: en
  Register ACC (.D(multiplexer_5_out), .Q(ACC_q), .clk(decoder_1_out3));  // open: en, clr

  // Other names for the same wires on the sheet: HALT = DONE

  // Notes on the sheet:
  //   contents of rom_1 (hex, n*v repeats v):
  //   8f 6 8f 5e 6 8f 5e 6 85 5f e 80 9b 7 81 5e 6 7e 1 81 5e 6 8f 7 8f 5e 6 82 5e 78 2 80 42 eb 80 1 83
  //   5e 2 71 a 8b 9a 7 82 5e 78 2 81 42 eb 81 1 83 5e 2 71 a 8b 9a 7 8f 5e 6 83 5e 78 2 81 60 1 81 59 5a
  //   1 8f 5e 6 71 e 8f 5e 6 85 5f e 88 91 7 81 5e 6 81 5e 6 7e 1 81 5e 6 71 3 8f 5e 6 8f 5e 6 73 e 84 5e
  //   78 2 82 60 1 81 59 5a 1 8f 5e 6 71 e 8f 5e 6 85 5f e 88 91 7 81 5e 6 81 5e 6 7e 3 81 5e 6 7e 1 81 5e
  //   6 80 5e 2 71 a 73 2 80 5e 78 5a 1 83 5e 2 71 a 8b 9a 7 81 5e 6 7e 7 8f 5e 6 8d 90 1 8f 5e 6 71 e 8f
  //   5e 6 85 5f e 88 91 7 81 5e 6 81 5e 6 7e 1 81 5e 6 71 3 73 1 81 5e 2 71 a 8b 9d 7 7e 7
  //   ALU
endmodule
